// Digital circuit 1BITREG.dig as structural Verilog
module _1BITREG (
  input  Din,
  input  SEL,
  input  CLK,
  output Dout
);

  wire _1bregMO;

  Multiplexer multiplexer_1 (.sel(SEL), .in_0(Dout), .in_1(Din), .out(_1bregMO));
  D_FF d_ff_1 (.D(_1bregMO), .C(CLK), .Q(Dout));  // open: nQ

  // Other names for the same wires on the sheet: _1bregCLK = CLK; _1bregDin = Din; _1bregDout = Dout; _1bregSEL = SEL
endmodule
