// Digital circuit 1x15RAM.dig as structural Verilog
module _1x15RAM (
  input  _1x15RamRS1,
  input  _1x15RamRS2,
  input  _1x15RamWS,
  input  [14:0] _1x15RamWD_14_0,
  input  _1x15RamCLK,
  output [14:0] _1x15RamRD1_14_0,
  output [14:0] _1x15RamRD2_14_0
);

  _1x1RAM _1x1ram_1 (
    .WD(_1x15RamWD_14_0[0]), .WS(_1x15RamWS), .RS1(_1x15RamRS1), .RS2(_1x15RamRS2), .CLK(_1x15RamCLK),
    .RD1(_1x15RamRD1_14_0[0]), .RD2(_1x15RamRD2_14_0[0]));
  _1x1RAM _1x1ram_2 (
    .WD(_1x15RamWD_14_0[1]), .WS(_1x15RamWS), .RS1(_1x15RamRS1), .RS2(_1x15RamRS2), .CLK(_1x15RamCLK),
    .RD1(_1x15RamRD1_14_0[1]), .RD2(_1x15RamRD2_14_0[1]));
  _1x1RAM _1x1ram_3 (
    .WD(_1x15RamWD_14_0[2]), .WS(_1x15RamWS), .RS1(_1x15RamRS1), .RS2(_1x15RamRS2), .CLK(_1x15RamCLK),
    .RD1(_1x15RamRD1_14_0[2]), .RD2(_1x15RamRD2_14_0[2]));
  _1x1RAM _1x1ram_4 (
    .WD(_1x15RamWD_14_0[3]), .WS(_1x15RamWS), .RS1(_1x15RamRS1), .RS2(_1x15RamRS2), .CLK(_1x15RamCLK),
    .RD1(_1x15RamRD1_14_0[3]), .RD2(_1x15RamRD2_14_0[3]));
  _1x1RAM _1x1ram_5 (
    .WD(_1x15RamWD_14_0[4]), .WS(_1x15RamWS), .RS1(_1x15RamRS1), .RS2(_1x15RamRS2), .CLK(_1x15RamCLK),
    .RD1(_1x15RamRD1_14_0[4]), .RD2(_1x15RamRD2_14_0[4]));
  _1x1RAM _1x1ram_6 (
    .WD(_1x15RamWD_14_0[5]), .WS(_1x15RamWS), .RS1(_1x15RamRS1), .RS2(_1x15RamRS2), .CLK(_1x15RamCLK),
    .RD1(_1x15RamRD1_14_0[5]), .RD2(_1x15RamRD2_14_0[5]));
  _1x1RAM _1x1ram_7 (
    .WD(_1x15RamWD_14_0[6]), .WS(_1x15RamWS), .RS1(_1x15RamRS1), .RS2(_1x15RamRS2), .CLK(_1x15RamCLK),
    .RD1(_1x15RamRD1_14_0[6]), .RD2(_1x15RamRD2_14_0[6]));
  _1x1RAM _1x1ram_8 (
    .WD(_1x15RamWD_14_0[7]), .WS(_1x15RamWS), .RS1(_1x15RamRS1), .RS2(_1x15RamRS2), .CLK(_1x15RamCLK),
    .RD1(_1x15RamRD1_14_0[7]), .RD2(_1x15RamRD2_14_0[7]));
  _1x1RAM _1x1ram_9 (
    .WD(_1x15RamWD_14_0[8]), .WS(_1x15RamWS), .RS1(_1x15RamRS1), .RS2(_1x15RamRS2), .CLK(_1x15RamCLK),
    .RD1(_1x15RamRD1_14_0[8]), .RD2(_1x15RamRD2_14_0[8]));
  _1x1RAM _1x1ram_10 (
    .WD(_1x15RamWD_14_0[9]), .WS(_1x15RamWS), .RS1(_1x15RamRS1), .RS2(_1x15RamRS2), .CLK(_1x15RamCLK),
    .RD1(_1x15RamRD1_14_0[9]), .RD2(_1x15RamRD2_14_0[9]));
  _1x1RAM _1x1ram_11 (
    .WD(_1x15RamWD_14_0[10]), .WS(_1x15RamWS), .RS1(_1x15RamRS1), .RS2(_1x15RamRS2), .CLK(_1x15RamCLK),
    .RD1(_1x15RamRD1_14_0[10]), .RD2(_1x15RamRD2_14_0[10]));
  _1x1RAM _1x1ram_12 (
    .WD(_1x15RamWD_14_0[11]), .WS(_1x15RamWS), .RS1(_1x15RamRS1), .RS2(_1x15RamRS2), .CLK(_1x15RamCLK),
    .RD1(_1x15RamRD1_14_0[11]), .RD2(_1x15RamRD2_14_0[11]));
  _1x1RAM _1x1ram_13 (
    .WD(_1x15RamWD_14_0[12]), .WS(_1x15RamWS), .RS1(_1x15RamRS1), .RS2(_1x15RamRS2), .CLK(_1x15RamCLK),
    .RD1(_1x15RamRD1_14_0[12]), .RD2(_1x15RamRD2_14_0[12]));
  _1x1RAM _1x1ram_14 (
    .WD(_1x15RamWD_14_0[13]), .WS(_1x15RamWS), .RS1(_1x15RamRS1), .RS2(_1x15RamRS2), .CLK(_1x15RamCLK),
    .RD1(_1x15RamRD1_14_0[13]), .RD2(_1x15RamRD2_14_0[13]));
  _1x1RAM _1x1ram_15 (
    .WD(_1x15RamWD_14_0[14]), .WS(_1x15RamWS), .RS1(_1x15RamRS1), .RS2(_1x15RamRS2), .CLK(_1x15RamCLK),
    .RD1(_1x15RamRD1_14_0[14]), .RD2(_1x15RamRD2_14_0[14]));

  // Other names for the same wires on the sheet: _1x15RamRD1_0 = _1x15RamRD1_14_0[0];
  //   _1x15RamRD1_1 = _1x15RamRD1_14_0[1]; _1x15RamRD1_2 = _1x15RamRD1_14_0[2]; _1x15RamRD1_3 = _1x15RamRD1_14_0[3];
  //   _1x15RamRD1_4 = _1x15RamRD1_14_0[4]; _1x15RamRD1_5 = _1x15RamRD1_14_0[5]; _1x15RamRD1_6 = _1x15RamRD1_14_0[6];
  //   _1x15RamRD1_7 = _1x15RamRD1_14_0[7]; _1x15RamRD1_8 = _1x15RamRD1_14_0[8]; _1x15RamRD1_9 = _1x15RamRD1_14_0[9];
  //   _1x15RamRD1_10 = _1x15RamRD1_14_0[10]; _1x15RamRD1_11 = _1x15RamRD1_14_0[11];
  //   _1x15RamRD1_12 = _1x15RamRD1_14_0[12]; _1x15RamRD1_13 = _1x15RamRD1_14_0[13];
  //   _1x15RamRD1_14 = _1x15RamRD1_14_0[14]; _1x15RamRD2_0 = _1x15RamRD2_14_0[0]; _1x15RamRD2_1 = _1x15RamRD2_14_0[1];
  //   _1x15RamRD2_2 = _1x15RamRD2_14_0[2]; _1x15RamRD2_3 = _1x15RamRD2_14_0[3]; _1x15RamRD2_4 = _1x15RamRD2_14_0[4];
  //   _1x15RamRD2_5 = _1x15RamRD2_14_0[5]; _1x15RamRD2_6 = _1x15RamRD2_14_0[6]; _1x15RamRD2_7 = _1x15RamRD2_14_0[7];
  //   _1x15RamRD2_8 = _1x15RamRD2_14_0[8]; _1x15RamRD2_9 = _1x15RamRD2_14_0[9]; _1x15RamRD2_10 = _1x15RamRD2_14_0[10];
  //   _1x15RamRD2_11 = _1x15RamRD2_14_0[11]; _1x15RamRD2_12 = _1x15RamRD2_14_0[12];
  //   _1x15RamRD2_13 = _1x15RamRD2_14_0[13]; _1x15RamRD2_14 = _1x15RamRD2_14_0[14]; _1x15RamWD0 = _1x15RamWD_14_0[0];
  //   _1x15RamWD1 = _1x15RamWD_14_0[1]; _1x15RamWD2 = _1x15RamWD_14_0[2]; _1x15RamWD3 = _1x15RamWD_14_0[3];
  //   _1x15RamWD4 = _1x15RamWD_14_0[4]; _1x15RamWD5 = _1x15RamWD_14_0[5]; _1x15RamWD6 = _1x15RamWD_14_0[6];
  //   _1x15RamWD7 = _1x15RamWD_14_0[7]; _1x15RamWD8 = _1x15RamWD_14_0[8]; _1x15RamWD9 = _1x15RamWD_14_0[9];
  //   _1x15RamWD10 = _1x15RamWD_14_0[10]; _1x15RamWD11 = _1x15RamWD_14_0[11]; _1x15RamWD12 = _1x15RamWD_14_0[12];
  //   _1x15RamWD13 = _1x15RamWD_14_0[13]; _1x15RamWD14 = _1x15RamWD_14_0[14]
endmodule
