// Digital circuit 1x1RAM.dig as structural Verilog
module _1x1RAM (
  input  WD,
  input  WS,
  input  CLK,
  input  RS1,
  input  RS2,
  output RD1,
  output RD2
);

  wire _1x1RamDout, _1x1RamMO;

  D_FF d_ff_1 (.D(_1x1RamMO), .C(CLK), .Q(_1x1RamDout));  // open: nQ
  Multiplexer multiplexer_1 (.sel(WS), .in_0(_1x1RamDout), .in_1(WD), .out(_1x1RamMO));
  and and_1 (RD1, _1x1RamDout, RS1);
  and and_2 (RD2, _1x1RamDout, RS2);

  // Other names for the same wires on the sheet: _1x1RamCLK = CLK; _1x1RamRD1 = RD1; _1x1RamRD2 = RD2;
  //   _1x1RamRS1 = RS1; _1x1RamRS2 = RS2; _1x1RamWD = WD; _1x1RamWS = WS
endmodule
