// Digital circuit 4bPC.dig as structural Verilog
module _4bPC (
  input  [3:0] I_3_0,
  input  PCCLOCK,
  output [3:0] O_3_0
);

  _1BITREG _1bitreg_1 (.Din(I_3_0[0]), .SEL(1'b1), .CLK(PCCLOCK), .Dout(O_3_0[0]));
  _1BITREG _1bitreg_2 (.Din(I_3_0[1]), .SEL(1'b1), .CLK(PCCLOCK), .Dout(O_3_0[1]));
  _1BITREG _1bitreg_3 (.Din(I_3_0[2]), .SEL(1'b1), .CLK(PCCLOCK), .Dout(O_3_0[2]));
  _1BITREG _1bitreg_4 (.Din(I_3_0[3]), .SEL(1'b1), .CLK(PCCLOCK), .Dout(O_3_0[3]));

  // Other names for the same wires on the sheet: PCI0 = I_3_0[0]; PCI1 = I_3_0[1]; PCI2 = I_3_0[2]; PCI3 = I_3_0[3];
  //   PCCLK = PCCLOCK; PCO0 = O_3_0[0]; PCO1 = O_3_0[1]; PCO2 = O_3_0[2]; PCO3 = O_3_0[3]
endmodule
