// Digital circuit 5BITREG.dig as structural Verilog
module _5BITREG (
  input  [4:0] Din_4_0,
  input  SEL,
  input  CLK,
  output [4:0] Dout_4_0
);

  _1BITREG _1bitreg_1 (.Din(Din_4_0[0]), .SEL(SEL), .CLK(CLK), .Dout(Dout_4_0[0]));
  _1BITREG _1bitreg_2 (.Din(Din_4_0[1]), .SEL(SEL), .CLK(CLK), .Dout(Dout_4_0[1]));
  _1BITREG _1bitreg_3 (.Din(Din_4_0[2]), .SEL(SEL), .CLK(CLK), .Dout(Dout_4_0[2]));
  _1BITREG _1bitreg_4 (.Din(Din_4_0[3]), .SEL(SEL), .CLK(CLK), .Dout(Dout_4_0[3]));
  _1BITREG _1bitreg_5 (.Din(Din_4_0[4]), .SEL(SEL), .CLK(CLK), .Dout(Dout_4_0[4]));

  // Other names for the same wires on the sheet: _5bregCLK = CLK; _5bregDout0 = Dout_4_0[0];
  //   _5bregDout1 = Dout_4_0[1]; _5bregDout2 = Dout_4_0[2]; _5bregDout3 = Dout_4_0[3]; _5bregDout4 = Dout_4_0[4];
  //   _5bregSEL = SEL; _5bregDin0 = Din_4_0[0]; _5bregDin1 = Din_4_0[1]; _5bregDin2 = Din_4_0[2];
  //   _5bregDin3 = Din_4_0[3]; _5bregDin4 = Din_4_0[4]
endmodule
