// Digital circuit 5BITREGSETWTH6REG.dig as structural Verilog
module _5BITREGSETWTH6REG (
  input  [2:0] Wr_2_0,
  input  REGEN,
  input  [4:0] WRD_4_0,
  input  CLK,
  input  [2:0] Ra_2_0,
  input  [2:0] Rb_2_0,
  output [4:0] A_4_0,
  output [4:0] B_4_0
);

  wire REGWRSEL0, REGWRSEL1, REGWRSEL2, REGWRSEL3, REGWRSEL4, REGWRSEL5, RS0, RS1, RS2, RS3, RS4, RS5;
  wire [4:0] REGRout0, REGRout1, REGRout2, REGRout3, REGRout4, REGRout5;

  Decoder #(.Selector_Bits(3)) decoder_1 (
    .sel(Wr_2_0), .out_0(RS0), .out_1(RS1), .out_2(RS2), .out_3(RS3), .out_4(RS4), .out_5(RS5));  // open: out_6, out_7
  and and_1 (REGWRSEL0, RS0, REGEN);
  and and_2 (REGWRSEL1, RS1, REGEN);
  and and_3 (REGWRSEL2, RS2, REGEN);
  and and_4 (REGWRSEL3, RS3, REGEN);
  and and_5 (REGWRSEL4, RS4, REGEN);
  and and_6 (REGWRSEL5, RS5, REGEN);
  _5BITREG _5bitreg_1 (.Din_4_0(WRD_4_0), .SEL(REGWRSEL0), .CLK(CLK), .Dout_4_0(REGRout0));
  _5BITREG _5bitreg_2 (.Din_4_0(WRD_4_0), .SEL(REGWRSEL1), .CLK(CLK), .Dout_4_0(REGRout1));
  _5BITREG _5bitreg_3 (.Din_4_0(WRD_4_0), .SEL(REGWRSEL2), .CLK(CLK), .Dout_4_0(REGRout2));
  _5BITREG _5bitreg_4 (.Din_4_0(WRD_4_0), .SEL(REGWRSEL3), .CLK(CLK), .Dout_4_0(REGRout3));
  _5BITREG _5bitreg_5 (.Din_4_0(WRD_4_0), .SEL(REGWRSEL4), .CLK(CLK), .Dout_4_0(REGRout4));
  _5BITREG _5bitreg_6 (.Din_4_0(WRD_4_0), .SEL(REGWRSEL5), .CLK(CLK), .Dout_4_0(REGRout5));
  Multiplexer #(.Selector_Bits(3), .Bits(5)) multiplexer_1 (
    .sel(Ra_2_0), .in_0(REGRout0), .in_1(REGRout1), .in_2(REGRout2), .in_3(REGRout3), .in_4(REGRout4),
    .in_5(REGRout5), .in_6({5{1'b0}}), .in_7({5{1'b0}}), .out(A_4_0));
  Multiplexer #(.Selector_Bits(3), .Bits(5)) multiplexer_2 (
    .sel(Rb_2_0), .in_0(REGRout0), .in_1(REGRout1), .in_2(REGRout2), .in_3(REGRout3), .in_4(REGRout4),
    .in_5(REGRout5), .in_6({5{1'b0}}), .in_7({5{1'b0}}), .out(B_4_0));

  // Other names for the same wires on the sheet: REGCLK = CLK; REGRa[2:0] = Ra_2_0; REGRaout[4:0] = A_4_0;
  //   REGRb[2:0] = Rb_2_0; REGRbout[4:0] = B_4_0; REGWRD[4:0] = WRD_4_0; WR[2:0] = Wr_2_0
endmodule
