// Digital circuit ADD.dig as structural Verilog
module ADD (
  input  [4:0] A_4_0,
  input  [4:0] B_4_0,
  input  Cin,
  output [4:0] R_4_0,
  output Cout
);

  wire ADDCout0, ADDCout1, ADDCout2, ADDCout3;

  FA fa_1 (.B(B_4_0[0]), .A(A_4_0[0]), .Cin(Cin), .S(R_4_0[0]), .Cout(ADDCout0));
  FA fa_2 (.B(B_4_0[1]), .A(A_4_0[1]), .Cin(ADDCout0), .S(R_4_0[1]), .Cout(ADDCout1));
  FA fa_3 (.B(B_4_0[2]), .A(A_4_0[2]), .Cin(ADDCout1), .S(R_4_0[2]), .Cout(ADDCout2));
  FA fa_4 (.B(B_4_0[3]), .A(A_4_0[3]), .Cin(ADDCout2), .S(R_4_0[3]), .Cout(ADDCout3));
  FA fa_5 (.B(B_4_0[4]), .A(A_4_0[4]), .Cin(ADDCout3), .S(R_4_0[4]), .Cout(Cout));

  // Other names for the same wires on the sheet: ADDA0 = A_4_0[0]; ADDA1 = A_4_0[1]; ADDA2 = A_4_0[2];
  //   ADDA3 = A_4_0[3]; ADDA4 = A_4_0[4]; ADDCin = Cin; ADDCout = Cout; ADDS0 = R_4_0[0]; ADDS1 = R_4_0[1];
  //   ADDS2 = R_4_0[2]; ADDS3 = R_4_0[3]; ADDS4 = R_4_0[4]; ADDB0 = B_4_0[0]; ADDB1 = B_4_0[1]; ADDB2 = B_4_0[2];
  //   ADDB3 = B_4_0[3]; ADDB4 = B_4_0[4]
endmodule
