// Digital circuit ALU.dig as structural Verilog
module ALU (
  input  [4:0] A_4_0,
  input  [4:0] B_4_0,
  input  [1:0] OP_1_0,
  output [4:0] R_4_0,
  output SF,
  output ZF
);

  wire [4:0] ALUADD, ALUOR, ALUSHL;

  ADD add_1 (.A_4_0(A_4_0), .B_4_0(B_4_0), .Cin(1'b0), .R_4_0(ALUADD));  // open: Cout
  OR or_1 (.A_4_0(A_4_0), .B_4_0(B_4_0), .R_4_0(ALUOR));
  SHL shl_1 (.A_4_0(A_4_0), .B_4_0(B_4_0), .R_4_0(ALUSHL));
  Multiplexer #(.Selector_Bits(2), .Bits(5)) multiplexer_1 (
    .sel(OP_1_0), .in_0(ALUADD), .in_1(ALUOR), .in_2(ALUSHL), .in_3({5{1'b0}}), .out(R_4_0));
  nor nor_1 (ZF, R_4_0[0], R_4_0[1], R_4_0[2], R_4_0[3], R_4_0[4]);

  assign SF = R_4_0[4];

  // Other names for the same wires on the sheet: ALUA[4:0] = A_4_0; ALUB[4:0] = B_4_0; ALUOP[1:0] = OP_1_0;
  //   ALUR[4:0] = R_4_0; ALUR0 = R_4_0[0]; ALUR1 = R_4_0[1]; ALUR2 = R_4_0[2]; ALUR3 = R_4_0[3]; ALUR4 = R_4_0[4];
  //   ALUZF = ZF
endmodule
