// Digital circuit CPU.dig as structural Verilog
module CPU (
  input  CLOCK,
  input  [3:0] WA_3_0,
  input  [14:0] WD_14_0,
  input  WE,
  input  PCEN,
  input  [3:0] RA2_3_0,
  output [14:0] RD1_14_0,
  output [14:0] RD2_14_0,
  output [4:0] A_4_0,
  output [4:0] B_4_0,
  output [2:0] REG_R1_2_0,
  output [2:0] REG_R2_2_0,
  output [4:0] R_4_0,
  output REG_EN,
  output IMM_SEL,
  output JMP_SEL,
  output [3:0] JMP_ADDR_3_0,
  output [3:0] currentRAM_LOCATION_3_0
);

  wire CPUCLK, CSF, CZF, Sf, Zf;
  wire [1:0] ALUop;
  wire [3:0] CPUPCI, CPUPCi_t;
  wire [4:0] CRB;

  PCADDER pcadder_1 (.I_3_0(currentRAM_LOCATION_3_0), .O_3_0(CPUPCi_t));
  _4bPC _4bpc_1 (.I_3_0(CPUPCI), .PCCLOCK(CPUCLK), .O_3_0(currentRAM_LOCATION_3_0));
  Multiplexer #(.Bits(4)) multiplexer_1 (.sel(JMP_SEL), .in_0(CPUPCi_t), .in_1(JMP_ADDR_3_0), .out(CPUPCI));
  and and_1 (CPUCLK, PCEN, CLOCK);
  RAM _10x15_RAM (
    .RA1_3_0(currentRAM_LOCATION_3_0), .RA2_3_0(RA2_3_0), .WA_3_0(WA_3_0), .WD_14_0(WD_14_0), .WE(WE),
    .CLK(CLOCK), .RD1_14_0({RD1_14_0[14:4], JMP_ADDR_3_0}), .RD2_14_0(RD2_14_0));
  CU cu_1 (
    .Opcode_4_0(RD1_14_0[14:11]), .SF(CSF), .ZF(CZF), .ALUop_1_0(ALUop), .REG_EN(REG_EN), .IMM_SEL(IMM_SEL),
    .JMP_SEL(JMP_SEL));
  _5BITREGSETWTH6REG _5bitregsetwth6reg_1 (
    .Wr_2_0(RD1_14_0[10:8]), .CLK(CPUCLK), .REGEN(REG_EN), .WRD_4_0(R_4_0), .Ra_2_0(RD1_14_0[10:8]),
    .Rb_2_0(RD1_14_0[7:5]), .A_4_0(A_4_0), .B_4_0(CRB));
  ALU alu_1 (.A_4_0(A_4_0), .B_4_0(B_4_0), .OP_1_0(ALUop), .R_4_0(R_4_0), .SF(Sf), .ZF(Zf));
  FLAGREG flagreg_1 (.CLK(CPUCLK), .SFi(Sf), .ZFi(Zf), .SF(CSF), .ZF(CZF));
  Multiplexer #(.Bits(5)) multiplexer_2 (.sel(IMM_SEL), .in_0(CRB), .in_1({RD1_14_0[4], JMP_ADDR_3_0}), .out(B_4_0));

  assign RD1_14_0[3:0] = JMP_ADDR_3_0;
  assign REG_R1_2_0 = RD1_14_0[10:8];
  assign REG_R2_2_0 = RD1_14_0[7:5];

  // Other names for the same wires on the sheet: CPUCLOCK = CLOCK; CPUPCEN = PCEN;
  //   CPUPCO[3:0] = currentRAM_LOCATION_3_0; CPUr[4:0] = R_4_0; CPURD1[14:0] = {RD1_14_0[14:4], JMP_ADDR_3_0};
  //   IMMV[4:0] = {RD1_14_0[4], JMP_ADDR_3_0}; JmpTO[3:0] = JMP_ADDR_3_0; DC = RD1_14_0[4]; R2[2:0] = RD1_14_0[7:5];
  //   R1[2:0] = RD1_14_0[10:8]; Opcode[3:0] = RD1_14_0[14:11]; CPURD2[14:0] = RD2_14_0; CPUWA[3:0] = WA_3_0;
  //   CPUWD[14:0] = WD_14_0; CPUWE = WE; CRA[4:0] = A_4_0; CRBf[4:0] = B_4_0; CREG_EN = REG_EN; immSEL = IMM_SEL;
  //   JmpSEL = JMP_SEL; RA2[3:0] = RA2_3_0
endmodule
