// Digital circuit CU.dig as structural Verilog
module CU (
  input  [3:0] Opcode_4_0,
  input  ZF,
  input  SF,
  output [1:0] ALUop_1_0,
  output REG_EN,
  output IMM_SEL,
  output JMP_SEL
);

  wire Cren0, Jmp, JmpS0, JmpS1, JmpS2;

  and and_1 (REG_EN, Cren0, Opcode_4_0[3]);
  nand nand_1 (Cren0, Opcode_4_0[0], Opcode_4_0[1]);
  and and_2 (IMM_SEL, Opcode_4_0[2], Opcode_4_0[3]);
  xor xor_1 (JMP_SEL, JmpS2, JmpS0);
  and and_3 (JmpS2, Jmp, JmpS1, Opcode_4_0[1]);
  or or_1 (JmpS1, SF, ZF);
  and and_4 (JmpS0, ~Opcode_4_0[1], Jmp);  // And
  nor nor_1 (Jmp, Opcode_4_0[2], Opcode_4_0[3]);

  assign ALUop_1_0 = Opcode_4_0[1:0];

  // Other names for the same wires on the sheet: Cren = REG_EN; CSF = SF; CZF = ZF; IMMSELECT = IMM_SEL;
  //   JmpSEL = JMP_SEL; ALUop[1:0] = Opcode_4_0[1:0]; O0 = Opcode_4_0[0]; O1 = Opcode_4_0[1]; T0 = Opcode_4_0[2];
  //   TOOP[1:0] = Opcode_4_0[3:2]; T1 = Opcode_4_0[3]
endmodule
