// Digital circuit FA.dig as structural Verilog
module FA (
  input  B,
  input  A,
  input  Cin,
  output S,
  output Cout
);

  wire FA_AxorB_andCin, FAAandB, FAAxorB;

  xor xor_1 (FAAxorB, A, B);
  and and_1 (FAAandB, B, A);
  xor xor_2 (S, FAAxorB, Cin);
  and and_2 (FA_AxorB_andCin, FAAxorB, Cin);
  or or_1 (Cout, FA_AxorB_andCin, FAAandB);

  // Other names for the same wires on the sheet: FAA = A; FAB = B; FACin = Cin; FACout = Cout; FAS = S
endmodule
