// Digital circuit FLAGREG.dig as structural Verilog
module FLAGREG (
  input  CLK,
  input  SFi,
  input  ZFi,
  output SF,
  output ZF
);

  _1BITREG SFREG (.Din(SFi), .SEL(1'b1), .CLK(CLK), .Dout(SF));
  _1BITREG ZFREG (.Din(ZFi), .SEL(1'b1), .CLK(CLK), .Dout(ZF));

  // Other names for the same wires on the sheet: FREGCLK = CLK; FREGSF = SFi; FREGSFout = SF; FREGZF = ZFi;
  //   FREGZFout = ZF
endmodule
