// Digital circuit OR.dig as structural Verilog
module OR (
  input  [4:0] A_4_0,
  input  [4:0] B_4_0,
  output [4:0] R_4_0
);

  or or_1 (R_4_0[0], A_4_0[0], B_4_0[0]);
  or or_2 (R_4_0[1], A_4_0[1], B_4_0[1]);
  or or_3 (R_4_0[2], A_4_0[2], B_4_0[2]);
  or or_4 (R_4_0[3], A_4_0[3], B_4_0[3]);
  or or_5 (R_4_0[4], A_4_0[4], B_4_0[4]);

  // Other names for the same wires on the sheet: ORA0 = A_4_0[0]; ORA1 = A_4_0[1]; ORA2 = A_4_0[2]; ORA3 = A_4_0[3];
  //   ORA4 = A_4_0[4]; ORB0 = B_4_0[0]; ORB1 = B_4_0[1]; ORB2 = B_4_0[2]; ORB3 = B_4_0[3]; ORB4 = B_4_0[4];
  //   ORR0 = R_4_0[0]; ORR1 = R_4_0[1]; ORR2 = R_4_0[2]; ORR3 = R_4_0[3]; ORR4 = R_4_0[4]
endmodule
