// Digital circuit PCADDER.dig as structural Verilog
module PCADDER (
  input  [3:0] I_3_0,
  output [3:0] O_3_0
);

  wire PCADDCout0, PCADDCout1, PCADDCout2, PCADDCout3;

  FA fa_1 (.B(1'b1), .A(I_3_0[0]), .Cin(1'b0), .S(O_3_0[0]), .Cout(PCADDCout0));
  FA fa_2 (.B(1'b0), .A(I_3_0[1]), .Cin(PCADDCout0), .S(O_3_0[1]), .Cout(PCADDCout1));
  FA fa_3 (.B(1'b0), .A(I_3_0[2]), .Cin(PCADDCout1), .S(O_3_0[2]), .Cout(PCADDCout2));
  FA fa_4 (.B(1'b0), .A(I_3_0[3]), .Cin(PCADDCout2), .S(O_3_0[3]), .Cout(PCADDCout3));

  // Other names for the same wires on the sheet: PCADDA0 = I_3_0[0]; PCADDA1 = I_3_0[1]; PCADDA2 = I_3_0[2];
  //   PCADDA3 = I_3_0[3]; PCADDS0 = O_3_0[0]; PCADDS1 = O_3_0[1]; PCADDS2 = O_3_0[2]; PCADDS3 = O_3_0[3]
endmodule
