// Digital circuit RAM.dig as structural Verilog
module RAM (
  input  [3:0] RA1_3_0,
  input  [3:0] RA2_3_0,
  input  [3:0] WA_3_0,
  input  [14:0] WD_14_0,
  input  WE,
  input  CLK,
  output [14:0] RD1_14_0,
  output [14:0] RD2_14_0
);

  wire RAMRA1_0, RAMRA1_1, RAMRA1_2, RAMRA1_3, RAMRA1_4, RAMRA1_5, RAMRA1_6, RAMRA1_7, RAMRA1_8, RAMRA1_9,
       RAMRA2_0, RAMRA2_1, RAMRA2_2, RAMRA2_3, RAMRA2_4, RAMRA2_5, RAMRA2_6, RAMRA2_7, RAMRA2_8, RAMRA2_9,
       RAMW0, RAMW1, RAMW2, RAMW3, RAMW4, RAMW5, RAMW6, RAMW7, RAMW8, RAMW9, RAMWA0, RAMWA1, RAMWA2, RAMWA3,
       RAMWA4, RAMWA5, RAMWA6, RAMWA7, RAMWA8, RAMWA9;
  wire [14:0] RAMRD1_0, RAMRD1_1, RAMRD1_2, RAMRD1_3, RAMRD1_4, RAMRD1_5, RAMRD1_6, RAMRD1_7, RAMRD1_8,
       RAMRD1_9, RAMRD2_0, RAMRD2_1, RAMRD2_2, RAMRD2_3, RAMRD2_4, RAMRD2_5, RAMRD2_6, RAMRD2_7, RAMRD2_8,
       RAMRD2_9;

  Decoder #(.Selector_Bits(4)) decoder_1 (
    .sel(WA_3_0), .out_0(RAMWA0), .out_1(RAMWA1), .out_2(RAMWA2), .out_3(RAMWA3), .out_4(RAMWA4),
    .out_5(RAMWA5), .out_6(RAMWA6), .out_7(RAMWA7), .out_8(RAMWA8), .out_9(RAMWA9));  // open: out_10, out_11, out_12, out_13, out_14, out_15
  and and_1 (RAMW0, RAMWA0, WE);
  and and_2 (RAMW1, RAMWA1, WE);
  and and_3 (RAMW2, RAMWA2, WE);
  and and_4 (RAMW3, RAMWA3, WE);
  and and_5 (RAMW4, RAMWA4, WE);
  and and_6 (RAMW5, RAMWA5, WE);
  and and_7 (RAMW6, RAMWA6, WE);
  and and_8 (RAMW7, RAMWA7, WE);
  and and_9 (RAMW8, RAMWA8, WE);
  and and_10 (RAMW9, RAMWA9, WE);
  Decoder #(.Selector_Bits(4)) decoder_2 (
    .sel(RA1_3_0), .out_0(RAMRA1_0), .out_1(RAMRA1_1), .out_2(RAMRA1_2), .out_3(RAMRA1_3), .out_4(RAMRA1_4),
    .out_5(RAMRA1_5), .out_6(RAMRA1_6), .out_7(RAMRA1_7), .out_8(RAMRA1_8), .out_9(RAMRA1_9));  // open: out_10, out_11, out_12, out_13, out_14, out_15
  Decoder #(.Selector_Bits(4)) decoder_3 (
    .sel(RA2_3_0), .out_0(RAMRA2_0), .out_1(RAMRA2_1), .out_2(RAMRA2_2), .out_3(RAMRA2_3), .out_4(RAMRA2_4),
    .out_5(RAMRA2_5), .out_6(RAMRA2_6), .out_7(RAMRA2_7), .out_8(RAMRA2_8), .out_9(RAMRA2_9));  // open: out_10, out_11, out_12, out_13, out_14, out_15
  _1x15RAM _1x15ram_1 (
    ._1x15RamRS1(RAMRA1_0), ._1x15RamRS2(RAMRA2_0), ._1x15RamWS(RAMW0), ._1x15RamWD_14_0(WD_14_0),
    ._1x15RamCLK(CLK), ._1x15RamRD1_14_0(RAMRD1_0), ._1x15RamRD2_14_0(RAMRD2_0));
  _1x15RAM _1x15ram_2 (
    ._1x15RamRS1(RAMRA1_1), ._1x15RamRS2(RAMRA2_1), ._1x15RamWS(RAMW1), ._1x15RamWD_14_0(WD_14_0),
    ._1x15RamCLK(CLK), ._1x15RamRD1_14_0(RAMRD1_1), ._1x15RamRD2_14_0(RAMRD2_1));
  _1x15RAM _1x15ram_3 (
    ._1x15RamRS1(RAMRA1_2), ._1x15RamRS2(RAMRA2_2), ._1x15RamWS(RAMW2), ._1x15RamWD_14_0(WD_14_0),
    ._1x15RamCLK(CLK), ._1x15RamRD1_14_0(RAMRD1_2), ._1x15RamRD2_14_0(RAMRD2_2));
  _1x15RAM _1x15ram_4 (
    ._1x15RamRS1(RAMRA1_3), ._1x15RamRS2(RAMRA2_3), ._1x15RamWS(RAMW3), ._1x15RamWD_14_0(WD_14_0),
    ._1x15RamCLK(CLK), ._1x15RamRD1_14_0(RAMRD1_3), ._1x15RamRD2_14_0(RAMRD2_3));
  _1x15RAM _1x15ram_5 (
    ._1x15RamRS1(RAMRA1_4), ._1x15RamRS2(RAMRA2_4), ._1x15RamWS(RAMW4), ._1x15RamWD_14_0(WD_14_0),
    ._1x15RamCLK(CLK), ._1x15RamRD1_14_0(RAMRD1_4), ._1x15RamRD2_14_0(RAMRD2_4));
  _1x15RAM _1x15ram_6 (
    ._1x15RamRS1(RAMRA1_5), ._1x15RamRS2(RAMRA2_5), ._1x15RamWS(RAMW5), ._1x15RamWD_14_0(WD_14_0),
    ._1x15RamCLK(CLK), ._1x15RamRD1_14_0(RAMRD1_5), ._1x15RamRD2_14_0(RAMRD2_5));
  _1x15RAM _1x15ram_7 (
    ._1x15RamRS1(RAMRA1_6), ._1x15RamRS2(RAMRA2_6), ._1x15RamWS(RAMW6), ._1x15RamWD_14_0(WD_14_0),
    ._1x15RamCLK(CLK), ._1x15RamRD1_14_0(RAMRD1_6), ._1x15RamRD2_14_0(RAMRD2_6));
  _1x15RAM _1x15ram_8 (
    ._1x15RamRS1(RAMRA1_7), ._1x15RamRS2(RAMRA2_7), ._1x15RamWS(RAMW7), ._1x15RamWD_14_0(WD_14_0),
    ._1x15RamCLK(CLK), ._1x15RamRD1_14_0(RAMRD1_7), ._1x15RamRD2_14_0(RAMRD2_7));
  _1x15RAM _1x15ram_9 (
    ._1x15RamRS1(RAMRA1_8), ._1x15RamRS2(RAMRA2_8), ._1x15RamWS(RAMW8), ._1x15RamWD_14_0(WD_14_0),
    ._1x15RamCLK(CLK), ._1x15RamRD1_14_0(RAMRD1_8), ._1x15RamRD2_14_0(RAMRD2_8));
  _1x15RAM _1x15ram_10 (
    ._1x15RamRS1(RAMRA1_9), ._1x15RamRS2(RAMRA2_9), ._1x15RamWS(RAMW9), ._1x15RamWD_14_0(WD_14_0),
    ._1x15RamCLK(CLK), ._1x15RamRD1_14_0(RAMRD1_9), ._1x15RamRD2_14_0(RAMRD2_9));
  assign RD1_14_0 = RAMRD1_0 | RAMRD1_1 | RAMRD1_2 | RAMRD1_3 | RAMRD1_4 | RAMRD1_5 | RAMRD1_6 | RAMRD1_7 | RAMRD1_8 | RAMRD1_9;  // Or or_1, 15 bits wide
  assign RD2_14_0 = RAMRD2_0 | RAMRD2_1 | RAMRD2_2 | RAMRD2_3 | RAMRD2_4 | RAMRD2_5 | RAMRD2_6 | RAMRD2_7 | RAMRD2_8 | RAMRD2_9;  // Or or_2, 15 bits wide

  // Other names for the same wires on the sheet: RAMCLK = CLK; RAMRA1[3:0] = RA1_3_0; RAMRA2[3:0] = RA2_3_0;
  //   RAMRD1[14:0] = RD1_14_0; RAMRD2[14:0] = RD2_14_0; RAMWA[3:0] = WA_3_0; RAMWD[14:0] = WD_14_0; RAMWE = WE
endmodule
